# Fritzing sketch bus Fritz 3 (saved by Fritzing 0.9.9b)
breadboards: 1

parts:
  Argon1 = Particle Argon
  HC-SR04_Sensor_1 = HC-SR04 Ultrasonic Distance Sensor
  U1 = MLX90614 [package=to-39]
  Grove1 = Grove Dust Sensor  # not connected
  Part1 = BME280 Breakout  # not connected
  U2 = AQ_Sensor [package=mq-3]

nets:
  N1: Argon1.A1, HC-SR04_Sensor_1.TRIG
  N2: Argon1.A2, U2.GND
  N3: Argon1.D6, U2.Vcc
  N4: Argon1.D8, U1.SCL_VZ
  VCC: Argon1.VUSB, HC-SR04_Sensor_1.VCC, U1.VDD, U2.Aout
  GND: HC-SR04_Sensor_1.GND, U1.VSS, U2.NC

custom parts:
  Particle Argon: The Argon is a powerful Wi-Fi enabled development board that can act as either a standalone Wi-Fi endpoint or Wi-Fi enabled gateway for Particle Mesh networks. It is based on the Nordic nRF52840 and has built-in battery charging circuitry so it’s easy to connect a Li-Po and deploy your local network in minutes. The Argon is great for connecting existing projects to the Particle Device Cloud or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
  Grove Dust Sensor: PPD42 Grove Dust Sensor
  AQ_Sensor: MQ-3 alcohol gas sensor . FP not tested. SEN-08880.
